# Fritzing sketch Hardware_v1 (saved by Fritzing 1.0.3b)
breadboards: 1

parts:
  Part1 = I2C level shifter bidirectional
  S1 = Adafruit 3104 lighted pushbutton [package=THT]
  U2 = 1v1-083 AliExpress RFID reader
  Part2 = ws2812b [package="smd 2812b"]
  Part3 = LCD1602-I2C
  KY-1 = Keyes Relay [package=THT]
  MH-ET_LIVE_ESP32_DEVKIT1 = MH-ET LIVE ESP32 DEVKIT 38 pins

nets:
  N1: Part1.LV4, MH-ET_LIVE_ESP32_DEVKIT1.IO27
  N2: Part1.LV3, MH-ET_LIVE_ESP32_DEVKIT1.IO23
  GND: Part1.GND, S1.pin_2, S1.pin_5, S1.pin_1, S1.pin_3, S1.pin_6, S1.pin_4, U2.Gnd, Part3.GND, MH-ET_LIVE_ESP32_DEVKIT1.IO32, MH-ET_LIVE_ESP32_DEVKIT1.GND#58, MH-ET_LIVE_ESP32_DEVKIT1.IO5
  VIN: Part1.LV, U2.Vin, KY-1.power, MH-ET_LIVE_ESP32_DEVKIT1.3V3
  N3: Part1.LV2, MH-ET_LIVE_ESP32_DEVKIT1.IO22
  N4: Part1.HV2, Part3.SDA
  VDD: Part1.HV, Part2.VDD, Part3.VCC, MH-ET_LIVE_ESP32_DEVKIT1.5V
  N5: Part1.HV3, Part3.SCL
  N6: Part1.HV4, Part2.DIN
  N7: U2.CST, MH-ET_LIVE_ESP32_DEVKIT1.IO25
  N8: U2.D0, MH-ET_LIVE_ESP32_DEVKIT1.IO16
  N9: U2.D1, MH-ET_LIVE_ESP32_DEVKIT1.IO4
  N10: Part2.VSS, KY-1.ground, MH-ET_LIVE_ESP32_DEVKIT1.GND#64
  N11: KY-1.signal, MH-ET_LIVE_ESP32_DEVKIT1.IO33

custom parts:
  Adafruit 3104 lighted pushbutton: This Mini Illuminated Momentary Power Button it an adorable breadboard-friendly tactile switch that has a built-in LED. It provides a simple way to add a tactile switch and a colorful universal power symbol to your project.
  1v1-083 AliExpress RFID reader: https://www.aliexpress.us/item/2255800841398634.html
  LCD1602-I2C: A standard character display, usually with 2x16 characters. Comes in many colors with LCM1602 IIC attached.
  Keyes Relay: The Keyes 5V relay module is suitable for SCM development, home appliance control. It uses a 5V~12V TIL control signal which can control DC / AC signal.
  MH-ET LIVE ESP32 DEVKIT 38 pins: http://mh.nodebb.com/topic/2/mh-et-live-esp32-devkit
